// Logisim project latch_ff.circ as structural Verilog
module main (
  input  NS_1,
  input  in_2,
  input  in_3,
  input  NR_1,
  input  D2,
  input  in_6,
  input  CLK_2,
  input  in_8,
  input  D3,
  input  clk3,
  input  in_11,
  input  in_12,
  input  J4,
  input  in_14,
  input  clk4,
  input  in_16,
  input  in_17,
  input  K4,
  input  clr4,
  input  J5,
  input  in_21,
  input  in_22,
  input  clk5,
  input  in_24,
  input  in_25,
  input  in_26,
  input  K5,
  input  set5,
  input  clr5,
  output Q_1,
  output out_31,
  output out_32,
  output out_33,
  output Q2,
  output out_35,
  output NQ2,
  output Q3,
  output out_38,
  output Qb3,
  output Q4,
  output out_41,
  output Qb4,
  output Q5,
  output out_44,
  output Qb5
);

  wire nand_1_out, nand_2_out, nand_3_out, nand_4_out, nand_5_out, nand_6_out, nand_7_out, nand_8_out,
       nand_9_out, nand_12_out, nand_13_out, nand_16_out, nand_17_out, nand_20_out, nand_21_out, not_1_out,
       not_2_out, not_3_out, not_4_out, not_5_out, not_6_out, not_7_out, not_8_out;

  not not_1 (not_1_out, D2);
  not not_2 (not_2_out, clk3);
  not not_3 (not_3_out, D3);
  nand nand_1 (nand_1_out, Qb4, J4, clk4);
  nand nand_2 (nand_2_out, clk4, K4, Q4);
  not not_4 (not_4_out, clr5);
  nor nor_1 (Q_1, NS_1, out_33);
  nor nor_2 (out_33, Q_1, NR_1);
  not not_5 (not_5_out, nand_1_out);
  not not_6 (not_6_out, clr4);
  nand nand_3 (nand_3_out, not_4_out, clk5, nand_4_out);
  nand nand_4 (nand_4_out, set5, not_4_out);
  nand nand_5 (nand_5_out, D2, CLK_2);
  nand nand_6 (nand_6_out, CLK_2, not_1_out);
  nand nand_7 (nand_7_out, D3, not_2_out);
  nand nand_8 (nand_8_out, not_2_out, not_3_out);
  not not_7 (not_7_out, nand_3_out);
  nand nand_9 (nand_9_out, not_5_out, not_6_out);
  nand nand_10 (Q2, nand_5_out, NQ2);
  nand nand_11 (NQ2, Q2, nand_6_out);
  nand nand_12 (nand_12_out, nand_7_out, nand_13_out);
  nand nand_13 (nand_13_out, nand_12_out, nand_8_out);
  nand nand_14 (Q4, nand_9_out, Qb4);
  nand nand_15 (Qb4, Q4, not_6_out, nand_2_out);
  nand nand_16 (nand_16_out, Qb5, J5, not_7_out);
  nand nand_17 (nand_17_out, not_7_out, K5, Q5);
  not not_8 (not_8_out, nand_12_out);
  nand nand_18 (Q5, nand_16_out, nand_4_out, Qb5);
  nand nand_19 (Qb5, Q5, not_4_out, nand_17_out);
  rs_latch rs_latch_1 (.s(in_2), .r(in_3), .q(out_31), .qb(out_32));
  nand nand_20 (nand_20_out, nand_12_out, clk3);
  nand nand_21 (nand_21_out, clk3, not_8_out);
  d_latch d_latch_1 (.clk(in_6), .d(in_8), .q(out_35));
  nand nand_22 (Q3, nand_20_out, Qb3);
  nand nand_23 (Qb3, Q3, nand_21_out);
  jk_flipflop jk_flipflop_1 (.clk(in_14), .j(in_16), .k(in_17), .q(out_41));
  jkff jkff_1 (.clk(in_21), .j(in_22), .k(in_24), .clr(in_25), .set(in_26), .q(out_44));
  d_flipflop d_flipflop_1 (.clk(in_11), .d(in_12), .q(out_38));

  // Notes on the sheet:
  //   1. RS Latch
  //   2. D Latch
  //   3. D Flip-Flop
  //   4. JK Flip-Flop 
  //   5. JK Flip-Flop with async Clear / Set
endmodule

// VHDL entity rs_latch, as the project stores it:
LIBRARY ieee;
USE ieee.std_logic_1164.ALL;

ENTITY rs_latch IS
  PORT (
    s  : IN  std_logic;   -- Set
    r  : IN  std_logic;   -- Reset
    q  : OUT std_logic;
    qb : OUT std_logic
  );
END rs_latch;

ARCHITECTURE bhv OF rs_latch IS
  SIGNAL q_int, qb_int : std_logic;
BEGIN
  -- Cross-coupled NOR gates (same as the Logisim circuit)
  q_int  <= r NOR qb_int;
  qb_int <= s NOR q_int;

  q  <= q_int;
  qb <= qb_int;
END bhv;

// VHDL entity d_latch, as the project stores it:
LIBRARY ieee;
USE ieee.std_logic_1164.ALL;

ENTITY d_latch IS
PORT (
    clk : IN std_logic;
    d   : IN std_logic;
    q   : OUT std_logic
);
END d_latch;

ARCHITECTURE bhv OF d_latch IS
BEGIN

    PROCESS(clk, d)
    BEGIN
        IF (clk = '1') THEN
            q <= d;
        END IF;
    END PROCESS;

END bhv;

// VHDL entity d_flipflop, as the project stores it:
LIBRARY ieee;
USE ieee.std_logic_1164.ALL;

ENTITY d_flipflop IS
  PORT (
    clk : IN std_logic;
    d   : IN std_logic;
    q   : OUT std_logic
  );
END d_flipflop;


ARCHITECTURE bhv OF d_flipflop IS
BEGIN
  process(clk)
  BEGIN
    IF (clk'event AND clk = '1') THEN
      q <= d;
    END IF;
  END process;
END bhv;

// VHDL entity jk_flipflop, as the project stores it:
LIBRARY ieee;
USE ieee.std_logic_1164.all;
USE ieee.numeric_std.all;

ENTITY jk_flipflop IS
  PORT (
    clk : IN  std_logic;  -- Clock signal
    j   : IN  std_logic;  -- Data input
    k   : IN  std_logic;  -- Data input
    q   : OUT std_logic   -- Data output
  );
END ENTITY jk_flipflop;

ARCHITECTURE bhv OF jk_flipflop IS
  SIGNAL q_internal : std_logic := '0';  -- Internal signal to represent output q
BEGIN
  -- Drive the output port q with the internal signal
  q <= q_internal;
  process(clk)
  begin
    -- Clock edge-triggered behavior
    if (clk'event and clk = '1') then
      if (j = '1' and k = '0') then
        q_internal <= '1';  -- Set output to 1
      elsif (j = '0' and k = '1') then
        q_internal <= '0';  -- Reset output to 0
      elsif (j = '1' and k = '1') then
        q_internal <= not q_internal;  -- Toggle the output
      end if; -- Close if block
    end if; -- Close main if block
  end process;
END ARCHITECTURE bhv;

// VHDL entity jkff, as the project stores it:
LIBRARY ieee;
USE ieee.std_logic_1164.all;
USE ieee.numeric_std.all;

ENTITY jkff IS
  PORT (
    clk : IN  std_logic;  -- Clock signal
    j   : IN  std_logic;  -- Data input
    k   : IN  std_logic;  -- Data input
    clr : IN  std_logic;  -- Asynchronous clear signal
    set : IN  std_logic;  -- Asynchronous set signal
    q   : OUT std_logic   -- Data output
  );
END ENTITY jkff;

ARCHITECTURE bhv OF jkff IS
  SIGNAL q_internal : std_logic := '0';  -- Internal signal to represent output q
BEGIN
  -- Drive the output port q with the internal signal
  q <= q_internal;
  process(clk, clr, set)
  begin
    -- Asynchronous clear (highest priority)
    if clr = '1' then
      q_internal <= '0';
    -- Asynchronous set (second-highest priority)
    elsif set = '1' then
      q_internal <= '1';
    -- Clock edge-triggered behavior
    elsif (clk'event and clk = '1') then
      if (j = '1' and k = '0') then
        q_internal <= '1';  -- Set output to 1
      elsif (j = '0' and k = '1') then
        q_internal <= '0';  -- Reset output to 0
      elsif (j = '1' and k = '1') then
        q_internal <= not q_internal;  -- Toggle the output
      end if; -- Close if block
    end if; -- Close main if block
  end process;
END ARCHITECTURE bhv;
