// Logisim project tesk_1013.circ as structural Verilog
module main (
  input  in_1,
  input  in_2,
  input  in_3,
  input  in_4,
  input  in_5,
  input  in_6,
  input  in_7,
  input  in_8,
  input  in_9,
  input  in_10,
  input  in_11,
  input  in_12,
  input  in_13,
  input  [2:0] in_14,
  input  in_15,
  input  [2:0] in_16,
  output out_17,
  output out_18,
  output out_19
);

  wire a, a1, b, b1, c, c1, d, d1, dp, dp1, e, e1, f, f1, g, g1, voting_with_25_1_result;
  wire [14:0] dipswitch_2_sw15;
  wire [24:0] dipswitch_1_sw25;

  DipSwitch #(.number(25)) dipswitch_1 (
    .sw1(dipswitch_1_sw25[24]), .sw2(dipswitch_1_sw25[23]), .sw3(dipswitch_1_sw25[22]),
    .sw4(dipswitch_1_sw25[21]), .sw5(dipswitch_1_sw25[20]), .sw6(dipswitch_1_sw25[19]),
    .sw7(dipswitch_1_sw25[18]), .sw8(dipswitch_1_sw25[17]), .sw9(dipswitch_1_sw25[16]),
    .sw10(dipswitch_1_sw25[15]), .sw11(dipswitch_1_sw25[14]), .sw12(dipswitch_1_sw25[13]),
    .sw13(dipswitch_1_sw25[12]), .sw14(dipswitch_1_sw25[11]), .sw15(dipswitch_1_sw25[10]),
    .sw16(dipswitch_1_sw25[9]), .sw17(dipswitch_1_sw25[8]), .sw18(dipswitch_1_sw25[7]),
    .sw19(dipswitch_1_sw25[6]), .sw20(dipswitch_1_sw25[5]), .sw21(dipswitch_1_sw25[4]),
    .sw22(dipswitch_1_sw25[3]), .sw23(dipswitch_1_sw25[2]), .sw24(dipswitch_1_sw25[1]),
    .sw25(dipswitch_1_sw25[0]));
  _7_Segment_Display u_7_segment_display_1 (.g(g), .f(f), .a(a), .b(b), .e(e), .d(d), .c(c), .dp(dp));
  and_or_out and_or_out_1 (.a(in_1), .b(in_2), .c(in_3), .d(in_5), .out1(out_17), .out2(out_18));
  multiplexer_8_1 multiplexer_8_1_1 (
    .a(in_6), .b(in_7), .c(in_8), .d(in_9), .e(in_10), .f(in_11), .g(in_12), .h(in_13), .ch(in_14),
    .data(out_19));
  digital_letters digital_letters_1 (.en(in_15), .dat(in_16), .display({a, b, c, d, e, f, g, dp}));
  voting_with_25 voting_with_25_1 (.vt(dipswitch_1_sw25), .result(voting_with_25_1_result));
  DipSwitch #(.number(15)) dipswitch_2 (
    .sw1(dipswitch_2_sw15[14]), .sw2(dipswitch_2_sw15[13]), .sw3(dipswitch_2_sw15[12]),
    .sw4(dipswitch_2_sw15[11]), .sw5(dipswitch_2_sw15[10]), .sw6(dipswitch_2_sw15[9]),
    .sw7(dipswitch_2_sw15[8]), .sw8(dipswitch_2_sw15[7]), .sw9(dipswitch_2_sw15[6]),
    .sw10(dipswitch_2_sw15[5]), .sw11(dipswitch_2_sw15[4]), .sw12(dipswitch_2_sw15[3]),
    .sw13(dipswitch_2_sw15[2]), .sw14(dipswitch_2_sw15[1]), .sw15(dipswitch_2_sw15[0]));
  LED led_1 (.in(voting_with_25_1_result));
  _7_Segment_Display u_7_segment_display_2 (.g(g1), .f(f1), .a(a1), .b(b1), .e(e1), .d(d1), .c(c1), .dp(dp1));
  vote_display vote_display_1 (.en(in_4), .vt(dipswitch_2_sw15), .display({a1, b1, c1, d1, e1, f1, g1, dp1}));
endmodule

// VHDL entity and_or_out, as the project stores it:
--------------------------------------------------------------------------------
-- Description : 
-- 1, Write VHDL code.
-- 1)out1 <= a and b and c and d;
-- 2)out2 <= a or b or c or d;
--
--------------------------------------------------------------------------------

LIBRARY ieee;
USE ieee.std_logic_1164.all;
use ieee.std_logic_arith.all;
use ieee.std_logic_unsigned.all;


--entity
ENTITY and_or_out IS
  PORT (
        a, b, c, d : in std_logic;
        out1, out2 : out std_logic
    );
END and_or_out;  -- ENTITY are not absolutely necessary! END; 가능

--architecture
architecture bhv of and_or_out is
begin
    out1 <= a and b and c and d;
    out2 <= a or b or c or d;
end architecture bhv;

// VHDL entity multiplexer_8_1, as the project stores it:
--------------------------------------------------------------------------------
-- Description :
-- 8-to-1 Multiplexer
--------------------------------------------------------------------------------
-- ch.. 8개니까 2^3... 000 001 010 011 ...
-- 
-- 
-- 
-- 
--------------------------------------------------------------------------------

LIBRARY ieee;
USE ieee.std_logic_1164.all;
use ieee.std_logic_arith.all;
use ieee.std_logic_unsigned.all;

--entity
ENTITY multiplexer_8_1 IS
  PORT (
        a, b, c, d, e, f, g, h : in std_logic;
        ch : in std_logic_vector(2 downto 0);
        data : out std_logic
    );
END multiplexer_8_1;

--arcitecture
ARCHITECTURE bhv OF multiplexer_8_1 IS
BEGIN
    process(a, b, c, d, e, f, g, h, ch)
    begin
        case ch is
            when "000" => data <= a;
            when "001" => data <= b;
            when "010" => data <= c;
            when "011" => data <= d;
            when "100" => data <= e;
            when "101" => data <= f;
            when "110" => data <= g;
            when others => data <= '0';
        end case;
    end process;
END bhv;

// VHDL entity digital_letters, as the project stores it:
--------------------------------------------------------------------------------
-- Description :
-- Use digital tubes to display letters: a,b,c,d,f,g
--------------------------------------------------------------------------------


library ieee;
use ieee.std_logic_1164.all;
use ieee.std_logic_arith.all;
use ieee.std_logic_unsigned.all;

--entity
entity digital_letters is
    port (
        en : in std_logic;
        dat : in std_logic_vector(2 downto 0);
        display : out std_logic_vector(7 downto 0)
    );
end digital_letters;


--architecture
architecture bhv of digital_letters is
begin
    process(en, dat)
    begin
        if en = '0' then
            display <= "ZZZZZZZZ";
        else
            case dat is
                when "000" => display <= "11101110";  -- A
                when "001" => display <= "00111110";  -- b
                when "010" => display <= "10011100";  -- C
                when "011" => display <= "01111010";  -- d
                when "100" => display <= "10001110";  -- F
                when "101" => display <= "11110110";  -- g
                when others => display <= "00000000";
            end case;
        end if;
    end process;
end architecture bhv;

// VHDL entity voting_with_25, as the project stores it:
--------------------------------------------------------------------------------
-- Description :
--
--------------------------------------------------------------------------------

LIBRARY ieee;
USE ieee.std_logic_1164.all;
use ieee.std_logic_arith.all;
use ieee.std_logic_unsigned.all;


entity voting_with_25 is
    port (
        vt : in std_logic_vector(25 downto 1);
        result : out std_logic
    );
end entity voting_with_25;

--architecture
architecture bhv of voting_with_25 is
begin
    process(vt)
        variable sum : integer range 0 to 25;
    begin
        sum := 0;
        for i in 1 to 25 loop
            if (vt(i) = '1') then
                sum := sum + 1;
                if sum >= 13 then
                    result <= '1';
                else
                    result <= '0';
                end if;
            end if;
        end loop;
    end process;
end architecture bhv;

// VHDL entity vote_display, as the project stores it:
library ieee;
use ieee.std_logic_1164.all;

--entity
entity vote_display is
    port (
        en      : in  std_logic;
        vt      : in  std_logic_vector(15 downto 1);
        display : out std_logic_vector(7 downto 0)
    );
end entity vote_display;

--architecture
architecture bhv of vote_display is
begin
    process(en, vt)
        variable sum : integer range 0 to 15;
    begin
        -- 1의 개수 세기
        sum := 0;
        for i in 1 to 15 loop
            if vt(i) = '1' then
                sum := sum + 1;
            end if;
        end loop;

        if en = '1' then
            -- en = '1' : 결과 표시
            case sum is
                when 0  => display <= "11111101";  -- 0
                when 1  => display <= "01100001";  -- 1
                when 2  => display <= "11011011";  -- 2
                when 3  => display <= "11110011";  -- 3
                when 4  => display <= "01100111";  -- 4
                when 5  => display <= "10110111";  -- 5
                when 6  => display <= "10111111";  -- 6
                when 7  => display <= "11100001";  -- 7
                when 8  => display <= "11111111";  -- 8
                when 9  => display <= "11110111";  -- 9
                when 10 => display <= "11101111";  -- A
                when 11 => display <= "00111111";  -- b (B)
                when 12 => display <= "10011101";  -- C
                when 13 => display <= "01111011";  -- d (D)
                when 14 => display <= "10011111";  -- E
                when 15 => display <= "10001111";  -- F
                when others => display <= "00000000";
            end case;
        else
            -- en = '0' (또는 그 외) : 꺼짐
            display <= "00000000";
        end if;
    end process;
end architecture bhv;
